// Logisim project MyALU.circ as structural Verilog: 8 circuits, main circuit ALU
module ALU (
  input  [15:0] a,
  input  [15:0] b,
  input  [2:0] Sel,
  output Overflow,
  output [15:0] Result
);

  wire [15:0] add_1_s, and16_1_r, mux16_1_r, or16_1_r;

  AND16 and16_1 (.r(and16_1_r), .a(a), .b(b));
  Add add_1 (.s(add_1_s), .signedOverflow(Overflow), .a(a), .b(b), .Sel(Sel[0]));
  OR16 or16_1 (.r(or16_1_r), .a(a), .b(b));
  MUX16 mux16_1 (.r(mux16_1_r), .b(or16_1_r), .Sel(Sel[1]), .a(and16_1_r));
  MUX16 mux16_2 (.r(Result), .b(mux16_1_r), .Sel(Sel[2]), .a(add_1_s));
endmodule

module oneBitAdder (
  input  ai,
  input  bi,
  input  c1,
  output si,
  output c2
);

  wire and_1_out, and_2_out, and_3_out;

  xor xor_1 (si, ai, c1, bi);
  and and_1 (and_1_out, bi, ai);
  and and_2 (and_2_out, bi, c1);
  and and_3 (and_3_out, ai, c1);
  or or_1 (c2, and_1_out, and_2_out, and_3_out);
endmodule

module Add (
  input  [15:0] a,
  input  [15:0] b,
  input  Sel,
  output [15:0] s,
  output signedOverflow
);

  wire onebitadder_1_c2, onebitadder_2_c2, onebitadder_3_c2, onebitadder_4_c2, onebitadder_5_c2,
       onebitadder_6_c2, onebitadder_7_c2, onebitadder_8_c2, onebitadder_9_c2, onebitadder_10_c2,
       onebitadder_11_c2, onebitadder_12_c2, onebitadder_13_c2, onebitadder_14_c2, onebitadder_15_c2,
       onebitadder_16_c2, xor_1_out, xor_3_out, xor_4_out, xor_5_out, xor_6_out, xor_7_out, xor_8_out,
       xor_9_out, xor_10_out, xor_11_out, xor_12_out, xor_13_out, xor_14_out, xor_15_out, xor_16_out,
       xor_17_out;

  oneBitAdder onebitadder_1 (.si(s[15]), .c2(onebitadder_1_c2), .ai(a[15]), .bi(xor_1_out), .c1(onebitadder_2_c2));
  xor xor_1 (xor_1_out, b[15], Sel);
  oneBitAdder onebitadder_2 (.si(s[14]), .c2(onebitadder_2_c2), .ai(a[14]), .bi(xor_3_out), .c1(onebitadder_3_c2));
  xor xor_2 (signedOverflow, onebitadder_1_c2, onebitadder_2_c2);
  xor xor_3 (xor_3_out, b[14], Sel);
  oneBitAdder onebitadder_3 (.si(s[13]), .c2(onebitadder_3_c2), .ai(a[13]), .bi(xor_4_out), .c1(onebitadder_4_c2));
  xor xor_4 (xor_4_out, b[13], Sel);
  oneBitAdder onebitadder_4 (.si(s[12]), .c2(onebitadder_4_c2), .ai(a[12]), .bi(xor_5_out), .c1(onebitadder_5_c2));
  xor xor_5 (xor_5_out, b[12], Sel);
  oneBitAdder onebitadder_5 (.si(s[11]), .c2(onebitadder_5_c2), .ai(a[11]), .bi(xor_6_out), .c1(onebitadder_6_c2));
  xor xor_6 (xor_6_out, b[11], Sel);
  oneBitAdder onebitadder_6 (.si(s[10]), .c2(onebitadder_6_c2), .ai(a[10]), .bi(xor_7_out), .c1(onebitadder_7_c2));
  xor xor_7 (xor_7_out, b[10], Sel);
  oneBitAdder onebitadder_7 (.si(s[9]), .c2(onebitadder_7_c2), .ai(a[9]), .bi(xor_8_out), .c1(onebitadder_8_c2));
  xor xor_8 (xor_8_out, b[9], Sel);
  oneBitAdder onebitadder_8 (.si(s[8]), .c2(onebitadder_8_c2), .ai(a[8]), .bi(xor_9_out), .c1(onebitadder_9_c2));
  xor xor_9 (xor_9_out, b[8], Sel);
  oneBitAdder onebitadder_9 (.si(s[7]), .c2(onebitadder_9_c2), .ai(a[7]), .bi(xor_10_out), .c1(onebitadder_10_c2));
  xor xor_10 (xor_10_out, b[7], Sel);
  oneBitAdder onebitadder_10 (.si(s[6]), .c2(onebitadder_10_c2), .ai(a[6]), .bi(xor_11_out), .c1(onebitadder_11_c2));
  xor xor_11 (xor_11_out, b[6], Sel);
  oneBitAdder onebitadder_11 (.si(s[5]), .c2(onebitadder_11_c2), .ai(a[5]), .bi(xor_12_out), .c1(onebitadder_12_c2));
  xor xor_12 (xor_12_out, b[5], Sel);
  oneBitAdder onebitadder_12 (.si(s[4]), .c2(onebitadder_12_c2), .ai(a[4]), .bi(xor_13_out), .c1(onebitadder_13_c2));
  xor xor_13 (xor_13_out, b[4], Sel);
  oneBitAdder onebitadder_13 (.si(s[3]), .c2(onebitadder_13_c2), .ai(a[3]), .bi(xor_14_out), .c1(onebitadder_14_c2));
  xor xor_14 (xor_14_out, b[3], Sel);
  oneBitAdder onebitadder_14 (.si(s[2]), .c2(onebitadder_14_c2), .ai(a[2]), .bi(xor_15_out), .c1(onebitadder_15_c2));
  xor xor_15 (xor_15_out, b[2], Sel);
  oneBitAdder onebitadder_15 (.si(s[1]), .c2(onebitadder_15_c2), .ai(a[1]), .bi(xor_16_out), .c1(onebitadder_16_c2));
  xor xor_16 (xor_16_out, b[1], Sel);
  oneBitAdder onebitadder_16 (.si(s[0]), .c2(onebitadder_16_c2), .ai(a[0]), .bi(xor_17_out), .c1(Sel));
  xor xor_17 (xor_17_out, b[0], Sel);
endmodule

module MUX2 (
  input  a,
  input  b,
  input  Sel,
  output c
);

  wire and_1_out, and_2_out, not_1_out;

  and and_1 (and_1_out, a, not_1_out);
  not not_1 (not_1_out, Sel);
  and and_2 (and_2_out, b, Sel);
  or or_1 (c, and_1_out, and_2_out);
endmodule

module AND16 (
  input  [15:0] a,
  input  [15:0] b,
  output [15:0] r
);

  and and_1 (r[15], a[15], b[15]);
  and and_2 (r[14], a[14], b[14]);
  and and_3 (r[13], a[13], b[13]);
  and and_4 (r[12], a[12], b[12]);
  and and_5 (r[11], a[11], b[11]);
  and and_6 (r[10], a[10], b[10]);
  and and_7 (r[9], a[9], b[9]);
  and and_8 (r[8], a[8], b[8]);
  and and_9 (r[7], a[7], b[7]);
  and and_10 (r[6], a[6], b[6]);
  and and_11 (r[5], a[5], b[5]);
  and and_12 (r[4], a[4], b[4]);
  and and_13 (r[3], a[3], b[3]);
  and and_14 (r[2], a[2], b[2]);
  and and_15 (r[1], a[1], b[1]);
  and and_16 (r[0], a[0], b[0]);
endmodule

module OR16 (
  input  [15:0] a,
  input  [15:0] b,
  output [15:0] r
);

  or or_1 (r[15], a[15], b[15]);
  or or_2 (r[14], a[14], b[14]);
  or or_3 (r[13], a[13], b[13]);
  or or_4 (r[12], a[12], b[12]);
  or or_5 (r[11], a[11], b[11]);
  or or_6 (r[10], a[10], b[10]);
  or or_7 (r[9], a[9], b[9]);
  or or_8 (r[8], a[8], b[8]);
  or or_9 (r[7], a[7], b[7]);
  or or_10 (r[6], a[6], b[6]);
  or or_11 (r[5], a[5], b[5]);
  or or_12 (r[4], a[4], b[4]);
  or or_13 (r[3], a[3], b[3]);
  or or_14 (r[2], a[2], b[2]);
  or or_15 (r[1], a[1], b[1]);
  or or_16 (r[0], a[0], b[0]);
endmodule

module MUX4 (
  input  [1:0] in_1,
  input  [1:0] in_2,
  input  Sel0,
  input  Sel1,
  output r
);

  wire mux2_1_c, mux2_3_c;

  MUX2 mux2_1 (.c(mux2_1_c), .a(in_1[1]), .b(in_2[1]), .Sel(Sel0));
  MUX2 mux2_2 (.c(r), .a(mux2_3_c), .b(mux2_1_c), .Sel(Sel1));
  MUX2 mux2_3 (.c(mux2_3_c), .a(in_1[0]), .b(in_2[0]), .Sel(Sel0));
endmodule

module MUX16 (
  input  [15:0] a,
  input  [15:0] b,
  input  Sel,
  output [15:0] r
);

  MUX2 mux2_1 (.c(r[15]), .a(b[15]), .b(a[15]), .Sel(Sel));
  MUX2 mux2_2 (.c(r[14]), .a(b[14]), .b(a[14]), .Sel(Sel));
  MUX2 mux2_3 (.c(r[13]), .a(b[13]), .b(a[13]), .Sel(Sel));
  MUX2 mux2_4 (.c(r[12]), .a(b[12]), .b(a[12]), .Sel(Sel));
  MUX2 mux2_5 (.c(r[11]), .a(b[11]), .b(a[11]), .Sel(Sel));
  MUX2 mux2_6 (.c(r[10]), .a(b[10]), .b(a[10]), .Sel(Sel));
  MUX2 mux2_7 (.c(r[9]), .a(b[9]), .b(a[9]), .Sel(Sel));
  MUX2 mux2_8 (.c(r[8]), .a(b[8]), .b(a[8]), .Sel(Sel));
  MUX2 mux2_9 (.c(r[7]), .a(b[7]), .b(a[7]), .Sel(Sel));
  MUX2 mux2_10 (.c(r[6]), .a(b[6]), .b(a[6]), .Sel(Sel));
  MUX2 mux2_11 (.c(r[5]), .a(b[5]), .b(a[5]), .Sel(Sel));
  MUX2 mux2_12 (.c(r[4]), .a(b[4]), .b(a[4]), .Sel(Sel));
  MUX2 mux2_13 (.c(r[3]), .a(b[3]), .b(a[3]), .Sel(Sel));
  MUX2 mux2_14 (.c(r[2]), .a(b[2]), .b(a[2]), .Sel(Sel));
  MUX2 mux2_15 (.c(r[1]), .a(b[1]), .b(a[1]), .Sel(Sel));
  MUX2 mux2_16 (.c(r[0]), .a(b[0]), .b(a[0]), .Sel(Sel));
endmodule
