// Logisim project ex5.circ as structural Verilog: 7 circuits, main circuit rotr
module rotr (
  input  [15:0] A,
  input  [3:0] B,
  output [15:0] Out1
);

  wire [15:0] mux16_1_c, mux16_2_c, mux16_3_c, rot1_1_out_2, rot2_1_out_2, rot4_1_out_2, rot8_1_out_2;

  rot8 rot8_1 (.in_1(A), .out_2(rot8_1_out_2));
  MUX16 mux16_1 (.c(mux16_1_c), .a(A), .b(rot8_1_out_2), .Sel(B[3]));
  rot4 rot4_1 (.in_1(mux16_1_c), .out_2(rot4_1_out_2));
  MUX16 mux16_2 (.c(mux16_2_c), .a(mux16_1_c), .b(rot4_1_out_2), .Sel(B[2]));
  rot2 rot2_1 (.in_1(mux16_2_c), .out_2(rot2_1_out_2));
  MUX16 mux16_3 (.c(mux16_3_c), .a(mux16_2_c), .b(rot2_1_out_2), .Sel(B[1]));
  rot1 rot1_1 (.in_1(mux16_3_c), .out_2(rot1_1_out_2));
  MUX16 mux16_4 (.c(Out1), .a(mux16_3_c), .b(rot1_1_out_2), .Sel(B[0]));

  // Notes on the sheet:
  //   PUT CIRCUITRY HERE
endmodule

module rot8 (
  input  [15:0] in_1,
  output [15:0] out_2
);

  wire [15:0] rot4_1_out_2;

  rot4 rot4_1 (.in_1(in_1), .out_2(rot4_1_out_2));
  rot4 rot4_2 (.in_1(rot4_1_out_2), .out_2(out_2));

  // Notes on the sheet:
  //   PUT CIRCUITRY HERE
endmodule

module rot4 (
  input  [15:0] in_1,
  output [15:0] out_2
);

  wire [15:0] rot2_1_out_2;

  rot2 rot2_1 (.in_1(in_1), .out_2(rot2_1_out_2));
  rot2 rot2_2 (.in_1(rot2_1_out_2), .out_2(out_2));

  // Notes on the sheet:
  //   PUT CIRCUITRY HERE
endmodule

module rot2 (
  input  [15:0] in_1,
  output [15:0] out_2
);

  wire [15:0] rot1_1_out_2;

  rot1 rot1_1 (.in_1(in_1), .out_2(rot1_1_out_2));
  rot1 rot1_2 (.in_1(rot1_1_out_2), .out_2(out_2));

  // Notes on the sheet:
  //   PUT CIRCUITRY HERE
endmodule

module rot1 (
  input  [15:0] in_1,
  output [15:0] out_2
);


  assign out_2 = {in_1[0], in_1[15:1]};

  // Other names for the same wires on the sheet: A15 = in_1[15]; A0 = in_1[0]

  // Notes on the sheet:
  //   PUT CIRCUITRY HERE
endmodule

module MUX2 (
  input  a,
  input  b,
  input  Sel,
  output c
);

  wire and_1_out, and_2_out, not_1_out;

  not not_1 (not_1_out, Sel);
  and and_1 (and_1_out, a, not_1_out);
  and and_2 (and_2_out, b, Sel);
  or or_1 (c, and_1_out, and_2_out);
endmodule

module MUX16 (
  input  [15:0] a,
  input  Sel,
  input  [15:0] b,
  output [15:0] c
);

  MUX2 mux2_1 (.c(c[15]), .a(a[15]), .b(b[15]), .Sel(Sel));
  MUX2 mux2_2 (.c(c[14]), .a(a[14]), .b(b[14]), .Sel(Sel));
  MUX2 mux2_3 (.c(c[13]), .a(a[13]), .b(b[13]), .Sel(Sel));
  MUX2 mux2_4 (.c(c[12]), .a(a[12]), .b(b[12]), .Sel(Sel));
  MUX2 mux2_5 (.c(c[11]), .a(a[11]), .b(b[11]), .Sel(Sel));
  MUX2 mux2_6 (.c(c[10]), .a(a[10]), .b(b[10]), .Sel(Sel));
  MUX2 mux2_7 (.c(c[9]), .a(a[9]), .b(b[9]), .Sel(Sel));
  MUX2 mux2_8 (.c(c[8]), .a(a[8]), .b(b[8]), .Sel(Sel));
  MUX2 mux2_9 (.c(c[7]), .a(a[7]), .b(b[7]), .Sel(Sel));
  MUX2 mux2_10 (.c(c[6]), .a(a[6]), .b(b[6]), .Sel(Sel));
  MUX2 mux2_11 (.c(c[5]), .a(a[5]), .b(b[5]), .Sel(Sel));
  MUX2 mux2_12 (.c(c[4]), .a(a[4]), .b(b[4]), .Sel(Sel));
  MUX2 mux2_13 (.c(c[3]), .a(a[3]), .b(b[3]), .Sel(Sel));
  MUX2 mux2_14 (.c(c[2]), .a(a[2]), .b(b[2]), .Sel(Sel));
  MUX2 mux2_15 (.c(c[1]), .a(a[1]), .b(b[1]), .Sel(Sel));
  MUX2 mux2_16 (.c(c[0]), .a(a[0]), .b(b[0]), .Sel(Sel));
endmodule
